# Fritzing sketch diagram (saved by Fritzing 0.7.7b)
breadboards: 1

parts:
  Arduino1 = Arduino
  元件1 = Bluetooth Mate Silver
  S1 = Pushbutton [package="[THT]"]
  S2 = Pushbutton [package="[THT]"]
  S3 = Pushbutton [package="[THT]"]
  R2 = Resistor [tolerance=±5% resistance=220 package=THT]
  R3 = Resistor [tolerance=±5% resistance=220 package=THT]
  R4 = Resistor [tolerance=±5% resistance=220 package=THT]
  R5 = Rotary Potentiometer (Small) [maximum_resistance=100kΩ]

nets:
  N1: Arduino1.D10, S1.Pin_1, S1.Pin_2, R2.Pin_0
  N2: Arduino1.D9, S2.Pin_1, S2.Pin_2, R3.Pin_0
  N3: Arduino1.D8, S3.Pin_1, S3.Pin_2, R4.Pin_0
  N4: Arduino1.D1TX, 元件1.RX_5V
  N5: Arduino1.D0RX, 元件1.TX_5V
  +5V: Arduino1.+5V, 元件1.VCC, S1.Pin_3, S1.Pin_4, S2.Pin_3, S2.Pin_4, S3.Pin_3, S3.Pin_4, R5.leg1
  GND: Arduino1.GND, 元件1.GND, R2.Pin_1, R3.Pin_1, R4.Pin_1, R5.leg2
  N6: Arduino1.A2, R5.wiper
